# Fritzing sketch 5temploggers (saved by Fritzing 0.9.0b)
breadboards: 1

parts:
  Part1 = Arduino Uno (Rev3)
  U1 = TMP36 [package=to-92-kit]
  U2 = TMP36 [package=to-92-kit]
  U3 = TMP36 [package=to-92-kit]
  U4 = TMP36 [package=to-92-kit]
  U5 = TMP36 [package=to-92-kit]
  R1 = Resistor [tolerance=±5% resistance=220 package=THT]
  R2 = Resistor [tolerance=±5% resistance=220 package=THT]
  R3 = Resistor [tolerance=±5% resistance=220 package=THT]
  R4 = Resistor [tolerance=±5% resistance=220 package=THT]
  R5 = Resistor [tolerance=±5% resistance=220 package=THT]

nets:
  N1: Part1.D2, U1.VOUT, R1.Pin_1
  N2: Part1.D3_PWM, U3.VOUT, R2.Pin_1
  N3: Part1.D4, U4.VOUT, R3.Pin_1
  N4: Part1.D5_PWM, U5.VOUT, R4.Pin_1
  N5: Part1.D6_PWM, U2.VOUT, R5.Pin_1
  VCC: Part1.5V, U1.VCC, U2.VCC, U3.VCC, U4.VCC, U5.VCC, R1.Pin_0, R2.Pin_0, R3.Pin_0, R4.Pin_0, R5.Pin_0
  GND: Part1.GND, U1.GND, U2.GND, U3.GND, U4.GND, U5.GND
